// Logisim project Laboratorio1_Omar_Torres_Leidy_Casta├▒o.circ as structural Verilog: 4 circuits, main circuit main
module main (
  input  S,
  input  CLR,
  input  X,
  input  CLK_MANUAL
);

  wire A0, A1, A02, A2, A03, A12, A13, A22, A23, B0, B1, B02, B2, B03, B12, B13, B22, B23, C0, C1, C02, C2,
       C03, C12, C13, C22, C23, clock_1_out, D0, D1, D02, D2, D03, D12, D13, D22, D23, dec_bcd_7_seg_1_sa,
       dec_bcd_7_seg_1_sb, dec_bcd_7_seg_1_sc, dec_bcd_7_seg_1_sd, dec_bcd_7_seg_1_se, dec_bcd_7_seg_1_sf,
       dec_bcd_7_seg_1_sg, dec_bcd_7_seg_2_sa, dec_bcd_7_seg_2_sb, dec_bcd_7_seg_2_sc, dec_bcd_7_seg_2_sd,
       dec_bcd_7_seg_2_se, dec_bcd_7_seg_2_sf, dec_bcd_7_seg_2_sg, dec_bcd_7_seg_3_sa, dec_bcd_7_seg_3_sb,
       dec_bcd_7_seg_3_sc, dec_bcd_7_seg_3_sd, dec_bcd_7_seg_3_se, dec_bcd_7_seg_3_sf, dec_bcd_7_seg_3_sg,
       dec_bcd_7_seg_4_sa, dec_bcd_7_seg_4_sb, dec_bcd_7_seg_4_sc, dec_bcd_7_seg_4_sd, dec_bcd_7_seg_4_se,
       dec_bcd_7_seg_4_sf, dec_bcd_7_seg_4_sg, dec_bcd_7_seg_5_sa, dec_bcd_7_seg_5_sb, dec_bcd_7_seg_5_sc,
       dec_bcd_7_seg_5_sd, dec_bcd_7_seg_5_se, dec_bcd_7_seg_5_sf, dec_bcd_7_seg_5_sg, dec_bcd_7_seg_6_sa,
       dec_bcd_7_seg_6_sb, dec_bcd_7_seg_6_sc, dec_bcd_7_seg_6_sd, dec_bcd_7_seg_6_se, dec_bcd_7_seg_6_sf,
       dec_bcd_7_seg_6_sg, dec_bcd_7_seg_7_sa, dec_bcd_7_seg_7_sb, dec_bcd_7_seg_7_sc, dec_bcd_7_seg_7_sd,
       dec_bcd_7_seg_7_se, dec_bcd_7_seg_7_sf, dec_bcd_7_seg_7_sg, dec_bcd_7_seg_8_sa, dec_bcd_7_seg_8_sb,
       dec_bcd_7_seg_8_sc, dec_bcd_7_seg_8_sd, dec_bcd_7_seg_8_se, dec_bcd_7_seg_8_sf, dec_bcd_7_seg_8_sg,
       dec_bcd_7_seg_9_sa, dec_bcd_7_seg_9_sb, dec_bcd_7_seg_9_sc, dec_bcd_7_seg_9_sd, dec_bcd_7_seg_9_se,
       dec_bcd_7_seg_9_sf, dec_bcd_7_seg_9_sg, or_1_out, S1, S2, S3;

  _7_Segment_Display u_7_segment_display_1 (
    .g(dec_bcd_7_seg_1_sg), .f(dec_bcd_7_seg_1_sf), .a(dec_bcd_7_seg_1_sa), .b(dec_bcd_7_seg_1_sb),
    .e(dec_bcd_7_seg_1_se), .d(dec_bcd_7_seg_1_sd), .c(dec_bcd_7_seg_1_sc));  // open: dp
  _7_Segment_Display u_7_segment_display_2 (
    .g(dec_bcd_7_seg_2_sg), .f(dec_bcd_7_seg_2_sf), .a(dec_bcd_7_seg_2_sa), .b(dec_bcd_7_seg_2_sb),
    .e(dec_bcd_7_seg_2_se), .d(dec_bcd_7_seg_2_sd), .c(dec_bcd_7_seg_2_sc));  // open: dp
  _7_Segment_Display u_7_segment_display_3 (
    .g(dec_bcd_7_seg_3_sg), .f(dec_bcd_7_seg_3_sf), .a(dec_bcd_7_seg_3_sa), .b(dec_bcd_7_seg_3_sb),
    .e(dec_bcd_7_seg_3_se), .d(dec_bcd_7_seg_3_sd), .c(dec_bcd_7_seg_3_sc));  // open: dp
  Clock clock_1 (.out(clock_1_out));
  DEC_BCD_7_SEG dec_bcd_7_seg_1 (
    .D(D2), .C(C2), .B(B2), .A(A2), .sa(dec_bcd_7_seg_1_sa), .sb(dec_bcd_7_seg_1_sb),
    .sc(dec_bcd_7_seg_1_sc), .sd(dec_bcd_7_seg_1_sd), .se(dec_bcd_7_seg_1_se), .sf(dec_bcd_7_seg_1_sf),
    .sg(dec_bcd_7_seg_1_sg));
  DEC_BCD_7_SEG dec_bcd_7_seg_2 (
    .D(D22), .C(C22), .B(B22), .A(A22), .sa(dec_bcd_7_seg_2_sa), .sb(dec_bcd_7_seg_2_sb),
    .sc(dec_bcd_7_seg_2_sc), .sd(dec_bcd_7_seg_2_sd), .se(dec_bcd_7_seg_2_se), .sf(dec_bcd_7_seg_2_sf),
    .sg(dec_bcd_7_seg_2_sg));
  DEC_BCD_7_SEG dec_bcd_7_seg_3 (
    .D(D23), .C(C23), .B(B23), .A(A23), .sa(dec_bcd_7_seg_3_sa), .sb(dec_bcd_7_seg_3_sb),
    .sc(dec_bcd_7_seg_3_sc), .sd(dec_bcd_7_seg_3_sd), .se(dec_bcd_7_seg_3_se), .sf(dec_bcd_7_seg_3_sf),
    .sg(dec_bcd_7_seg_3_sg));
  or or_1 (or_1_out, CLK_MANUAL, clock_1_out);
  _7_Segment_Display u_7_segment_display_4 (
    .g(dec_bcd_7_seg_4_sg), .f(dec_bcd_7_seg_4_sf), .a(dec_bcd_7_seg_4_sa), .b(dec_bcd_7_seg_4_sb),
    .e(dec_bcd_7_seg_4_se), .d(dec_bcd_7_seg_4_sd), .c(dec_bcd_7_seg_4_sc));  // open: dp
  _7_Segment_Display u_7_segment_display_5 (
    .g(dec_bcd_7_seg_5_sg), .f(dec_bcd_7_seg_5_sf), .a(dec_bcd_7_seg_5_sa), .b(dec_bcd_7_seg_5_sb),
    .e(dec_bcd_7_seg_5_se), .d(dec_bcd_7_seg_5_sd), .c(dec_bcd_7_seg_5_sc));  // open: dp
  _7_Segment_Display u_7_segment_display_6 (
    .g(dec_bcd_7_seg_6_sg), .f(dec_bcd_7_seg_6_sf), .a(dec_bcd_7_seg_6_sa), .b(dec_bcd_7_seg_6_sb),
    .e(dec_bcd_7_seg_6_se), .d(dec_bcd_7_seg_6_sd), .c(dec_bcd_7_seg_6_sc));  // open: dp
  DEC_BCD_7_SEG dec_bcd_7_seg_4 (
    .D(D12), .C(C12), .B(B12), .A(A12), .sa(dec_bcd_7_seg_4_sa), .sb(dec_bcd_7_seg_4_sb),
    .sc(dec_bcd_7_seg_4_sc), .sd(dec_bcd_7_seg_4_sd), .se(dec_bcd_7_seg_4_se), .sf(dec_bcd_7_seg_4_sf),
    .sg(dec_bcd_7_seg_4_sg));
  DEC_BCD_7_SEG dec_bcd_7_seg_5 (
    .D(D13), .C(C13), .B(B13), .A(A13), .sa(dec_bcd_7_seg_5_sa), .sb(dec_bcd_7_seg_5_sb),
    .sc(dec_bcd_7_seg_5_sc), .sd(dec_bcd_7_seg_5_sd), .se(dec_bcd_7_seg_5_se), .sf(dec_bcd_7_seg_5_sf),
    .sg(dec_bcd_7_seg_5_sg));
  DEC_BCD_7_SEG dec_bcd_7_seg_6 (
    .D(D1), .C(C1), .B(B1), .A(A1), .sa(dec_bcd_7_seg_6_sa), .sb(dec_bcd_7_seg_6_sb),
    .sc(dec_bcd_7_seg_6_sc), .sd(dec_bcd_7_seg_6_sd), .se(dec_bcd_7_seg_6_se), .sf(dec_bcd_7_seg_6_sf),
    .sg(dec_bcd_7_seg_6_sg));
  _7_Segment_Display u_7_segment_display_7 (
    .g(dec_bcd_7_seg_7_sg), .f(dec_bcd_7_seg_7_sf), .a(dec_bcd_7_seg_7_sa), .b(dec_bcd_7_seg_7_sb),
    .e(dec_bcd_7_seg_7_se), .d(dec_bcd_7_seg_7_sd), .c(dec_bcd_7_seg_7_sc));  // open: dp
  _7_Segment_Display u_7_segment_display_8 (
    .g(dec_bcd_7_seg_8_sg), .f(dec_bcd_7_seg_8_sf), .a(dec_bcd_7_seg_8_sa), .b(dec_bcd_7_seg_8_sb),
    .e(dec_bcd_7_seg_8_se), .d(dec_bcd_7_seg_8_sd), .c(dec_bcd_7_seg_8_sc));  // open: dp
  Detector_Secuencias detector_secuencias_1 (.S(S), .CLK(or_1_out), .X(X), .CLR(CLR), .S1(S1), .S2(S2), .S3(S3));
  _7_Segment_Display u_7_segment_display_9 (
    .g(dec_bcd_7_seg_9_sg), .f(dec_bcd_7_seg_9_sf), .a(dec_bcd_7_seg_9_sa), .b(dec_bcd_7_seg_9_sb),
    .e(dec_bcd_7_seg_9_se), .d(dec_bcd_7_seg_9_sd), .c(dec_bcd_7_seg_9_sc));  // open: dp
  DEC_BCD_7_SEG dec_bcd_7_seg_7 (
    .D(D02), .C(C02), .B(B02), .A(A02), .sa(dec_bcd_7_seg_7_sa), .sb(dec_bcd_7_seg_7_sb),
    .sc(dec_bcd_7_seg_7_sc), .sd(dec_bcd_7_seg_7_sd), .se(dec_bcd_7_seg_7_se), .sf(dec_bcd_7_seg_7_sf),
    .sg(dec_bcd_7_seg_7_sg));
  DEC_BCD_7_SEG dec_bcd_7_seg_8 (
    .D(D03), .C(C03), .B(B03), .A(A03), .sa(dec_bcd_7_seg_8_sa), .sb(dec_bcd_7_seg_8_sb),
    .sc(dec_bcd_7_seg_8_sc), .sd(dec_bcd_7_seg_8_sd), .se(dec_bcd_7_seg_8_se), .sf(dec_bcd_7_seg_8_sf),
    .sg(dec_bcd_7_seg_8_sg));
  DEC_BCD_7_SEG dec_bcd_7_seg_9 (
    .D(D0), .C(C0), .B(B0), .A(A0), .sa(dec_bcd_7_seg_9_sa), .sb(dec_bcd_7_seg_9_sb),
    .sc(dec_bcd_7_seg_9_sc), .sd(dec_bcd_7_seg_9_sd), .se(dec_bcd_7_seg_9_se), .sf(dec_bcd_7_seg_9_sf),
    .sg(dec_bcd_7_seg_9_sg));
  Contador_binario contador_binario_1 (
    .S(1'b0), .JK(1'b1), .clk(S1), .CLR(CLR), .D1(D1), .C1(C1), .B1(B1), .A1(A1), .D0(D0), .C0(C0), .B0(B0),
    .A0(A0), .D2(D2), .C2(C2), .B2(B2), .A2(A2));
  Contador_binario contador_binario_2 (
    .S(1'b0), .JK(1'b1), .clk(S2), .CLR(CLR), .D1(D12), .C1(C12), .B1(B12), .A1(A12), .D0(D02), .C0(C02),
    .B0(B02), .A0(A02), .D2(D22), .C2(C22), .B2(B22), .A2(A22));
  Contador_binario contador_binario_3 (
    .S(1'b0), .JK(1'b1), .clk(S3), .CLR(CLR), .D1(D13), .C1(C13), .B1(B13), .A1(A13), .D0(D03), .C0(C03),
    .B0(B03), .A0(A03), .D2(D23), .C2(C23), .B2(B23), .A2(A23));

  // Notes on the sheet:
  //   1100
  //   10001
  //   110000
endmodule

module DEC_BCD_7_SEG (
  input  D,
  input  C,
  input  B,
  input  A,
  output sa,
  output sb,
  output sc,
  output sd,
  output se,
  output sf,
  output sg
);

  wire and_1_out, and_2_out, and_3_out, and_4_out, and_5_out, and_6_out, and_7_out, and_8_out, and_9_out,
       and_10_out, and_11_out, and_12_out, and_13_out, and_14_out, and_15_out, and_16_out, and_17_out,
       and_18_out, not_1_out, not_2_out, not_3_out, not_4_out;

  not not_1 (not_1_out, B);
  not not_2 (not_2_out, C);
  not not_3 (not_3_out, D);
  not not_4 (not_4_out, A);
  and and_1 (and_1_out, not_2_out, not_4_out);
  and and_2 (and_2_out, C, A);
  and and_3 (and_3_out, B, A);
  and and_4 (and_4_out, not_1_out, not_4_out);
  and and_5 (and_5_out, not_3_out, A);
  and and_6 (and_6_out, C, B);
  and and_7 (and_7_out, not_4_out, B);
  and and_8 (and_8_out, not_4_out, not_2_out);
  and and_9 (and_9_out, C, not_1_out, A);
  and and_10 (and_10_out, not_2_out, not_3_out, B);
  and and_11 (and_11_out, not_2_out, not_4_out);
  and and_12 (and_12_out, not_3_out, B, not_4_out);
  and and_13 (and_13_out, not_1_out, not_4_out);
  and and_14 (and_14_out, not_1_out, C);
  and and_15 (and_15_out, C, B, not_4_out);
  and and_16 (and_16_out, C, not_1_out);
  and and_17 (and_17_out, B, not_4_out);
  and and_18 (and_18_out, B, not_2_out, not_3_out);
  or or_1 (sa, and_1_out, and_2_out, D, B);
  or or_2 (sc, and_5_out, and_6_out, not_1_out, D);
  or or_3 (sd, and_7_out, and_8_out, D, and_9_out, and_10_out);
  or or_4 (sb, and_3_out, and_4_out, not_2_out, D);
  or or_5 (se, and_11_out, and_12_out);
  or or_6 (sf, and_13_out, and_14_out, and_15_out, D);
  or or_7 (sg, D, and_16_out, and_17_out, and_18_out);
endmodule

module Contador_binario (
  input  S,
  input  JK,
  input  clk,
  input  CLR,
  output D1,
  output C1,
  output B1,
  output A1,
  output D0,
  output C0,
  output B0,
  output A0,
  output D2,
  output C2,
  output B2,
  output A2
);

  wire and_1_out, and_2_out, and_3_out, j_k_ff_2_qn, j_k_ff_3_qn, j_k_ff_4_qn, j_k_ff_5_qn, j_k_ff_6_qn,
       j_k_ff_7_qn, j_k_ff_8_qn, j_k_ff_9_qn, j_k_ff_10_qn, j_k_ff_11_qn, j_k_ff_12_qn, or_1_out, or_2_out,
       or_3_out;

  J_K_Flip_Flop j_k_ff_1 (.J(JK), .K(JK), .clk(j_k_ff_2_qn), .Q(D2), .preset(S), .reset(or_1_out));  // open: Qn
  J_K_Flip_Flop j_k_ff_2 (.J(JK), .K(JK), .clk(j_k_ff_3_qn), .Q(C2), .Qn(j_k_ff_2_qn), .preset(S), .reset(or_1_out));
  or or_1 (or_1_out, and_1_out, CLR);
  J_K_Flip_Flop j_k_ff_3 (.J(JK), .K(JK), .clk(j_k_ff_4_qn), .Q(B2), .Qn(j_k_ff_3_qn), .preset(S), .reset(or_1_out));
  and and_1 (and_1_out, B2, D2);
  J_K_Flip_Flop j_k_ff_4 (.J(JK), .K(JK), .clk(j_k_ff_5_qn), .Q(A2), .Qn(j_k_ff_4_qn), .preset(S), .reset(or_1_out));
  J_K_Flip_Flop j_k_ff_5 (.J(JK), .K(JK), .clk(j_k_ff_6_qn), .Q(D1), .Qn(j_k_ff_5_qn), .preset(S), .reset(or_2_out));
  or or_2 (or_2_out, and_2_out, CLR);
  J_K_Flip_Flop j_k_ff_6 (.J(JK), .K(JK), .clk(j_k_ff_7_qn), .Q(C1), .Qn(j_k_ff_6_qn), .preset(S), .reset(or_2_out));
  and and_2 (and_2_out, B1, D1);
  J_K_Flip_Flop j_k_ff_7 (.J(JK), .K(JK), .clk(j_k_ff_8_qn), .Q(B1), .Qn(j_k_ff_7_qn), .preset(S), .reset(or_2_out));
  J_K_Flip_Flop j_k_ff_8 (.J(JK), .K(JK), .clk(j_k_ff_9_qn), .Q(A1), .Qn(j_k_ff_8_qn), .preset(S), .reset(or_2_out));
  J_K_Flip_Flop j_k_ff_9 (.J(JK), .K(JK), .clk(j_k_ff_10_qn), .Q(D0), .Qn(j_k_ff_9_qn), .preset(S), .reset(or_3_out));
  or or_3 (or_3_out, and_3_out, CLR);
  J_K_Flip_Flop j_k_ff_10 (.J(JK), .K(JK), .clk(j_k_ff_11_qn), .Q(C0), .Qn(j_k_ff_10_qn), .preset(S), .reset(or_3_out));
  and and_3 (and_3_out, B0, D0);
  J_K_Flip_Flop j_k_ff_11 (.J(JK), .K(JK), .clk(j_k_ff_12_qn), .Q(B0), .Qn(j_k_ff_11_qn), .preset(S), .reset(or_3_out));
  J_K_Flip_Flop j_k_ff_12 (.J(JK), .K(JK), .clk(clk), .Q(A0), .Qn(j_k_ff_12_qn), .preset(S), .reset(or_3_out));

  // Other names for the same wires on the sheet: X = CLR
endmodule

module Detector_Secuencias (
  input  S,
  input  CLK,
  input  X,
  input  CLR,
  output S1,
  output S2,
  output S3
);

  wire and_4_out, and_5_out, and_6_out, and_7_out, and_8_out, and_9_out, and_10_out, and_11_out, and_12_out,
       and_13_out, and_14_out, and_15_out, and_16_out, and_17_out, and_18_out, and_19_out, and_20_out,
       and_21_out, and_22_out, and_23_out, and_24_out, and_25_out, and_26_out, or_1_out, or_2_out, or_3_out,
       or_4_out, or_5_out, or_6_out, or_7_out, Q0, Q0_NEG, Q1, Q1_NEG, Q2, Q2_NEG, Q3, Q3_NEG, X_NEG;

  and and_1 (S1, Q3_NEG, Q2, Q1, Q0);
  and and_2 (S2, Q3, Q2_NEG, Q1, Q0_NEG);
  and and_3 (S3, Q3, Q2_NEG, Q1_NEG, Q0);
  not not_1 (X_NEG, X);
  and and_4 (and_4_out, Q3_NEG, Q2_NEG, X);
  and and_5 (and_5_out, Q3_NEG, Q1);
  and and_6 (and_6_out, Q3, Q1_NEG, X_NEG);
  and and_7 (and_7_out, Q3, Q2);
  and and_8 (and_8_out, Q1, X);
  and and_9 (and_9_out, Q3_NEG, Q0, X_NEG);
  and and_10 (and_10_out, Q3_NEG, Q2, Q0_NEG, X);
  and and_11 (and_11_out, Q3, Q2_NEG, Q0_NEG, X);
  and and_12 (and_12_out, Q3_NEG, Q1_NEG, Q0, X);
  and and_13 (and_13_out, Q3, Q1, Q0);
  and and_14 (and_14_out, Q1, Q0, X_NEG);
  and and_15 (and_15_out, Q1, X);
  and and_16 (and_16_out, Q3, X);
  and and_17 (and_17_out, Q3, Q0);
  and and_18 (and_18_out, Q1, Q0);
  and and_19 (and_19_out, Q3_NEG, Q1_NEG, Q0_NEG);
  and and_20 (and_20_out, Q2, Q1_NEG, Q0_NEG, X);
  and and_21 (and_21_out, Q2, Q1, Q0, X_NEG);
  and and_22 (and_22_out, Q0, X);
  and and_23 (and_23_out, Q2, X);
  and and_24 (and_24_out, Q1, Q0_NEG, X_NEG);
  and and_25 (and_25_out, Q2_NEG, Q1_NEG, Q0, X_NEG);
  or or_1 (or_1_out, and_4_out, and_5_out, and_6_out, and_7_out, and_8_out);
  or or_2 (or_2_out, and_9_out, and_10_out, and_11_out);
  and and_26 (and_26_out, Q3_NEG, X);
  or or_3 (or_3_out, and_12_out, and_13_out, and_14_out);
  or or_4 (or_4_out, and_15_out, and_16_out, and_17_out, and_18_out, and_19_out);
  or or_5 (or_5_out, and_20_out, and_21_out);
  or or_6 (or_6_out, and_22_out, and_23_out, and_24_out, and_25_out);
  J_K_Flip_Flop FF0 (.J(or_1_out), .K(X_NEG), .clk(CLK), .Q(Q0), .Qn(Q0_NEG), .preset(S), .reset(CLR));
  J_K_Flip_Flop FF1 (.J(or_2_out), .K(or_7_out), .clk(CLK), .Q(Q1), .Qn(Q1_NEG), .preset(S), .reset(CLR));
  or or_7 (or_7_out, and_26_out, Q0);
  J_K_Flip_Flop FF2 (.J(or_3_out), .K(or_4_out), .clk(CLK), .Q(Q2), .Qn(Q2_NEG), .preset(S), .reset(CLR));
  J_K_Flip_Flop FF3 (.J(or_5_out), .K(or_6_out), .clk(CLK), .Q(Q3), .Qn(Q3_NEG), .preset(S), .reset(CLR));
endmodule
